// Digital circuit Q2_6bitCnt.dig as structural Verilog
module Q2_6bitCnt (
  input  A_0,
  input  A_1,
  input  A_2,
  input  A_3,
  input  A_4,
  input  A_5,
  output [2:0] S
);

  wire [1:0] add_1_s, add_2_s;

  Add add_1 (.a(A_0), .b(A_1), .c_i(A_2), .s(add_1_s[0]), .c_o(add_1_s[1]));
  Add add_2 (.a(A_3), .b(A_4), .c_i(A_5), .s(add_2_s[0]), .c_o(add_2_s[1]));
  Add #(.Bits(2)) add_3 (.a(add_1_s), .b(add_2_s), .c_i(1'b0), .s(S[1:0]), .c_o(S[2]));
endmodule
