// Digital circuit Q2_9bitCnt.dig as structural Verilog
module Q2_9bitCnt (
  input  A_0,
  input  A_1,
  input  A_2,
  input  A_3,
  input  A_4,
  input  A_5,
  input  A_6,
  input  A_7,
  input  A_8,
  output [3:0] S
);

  wire [1:0] add_1_s, add_2_s, add_3_s, add_4_s, add_5_s;
  wire [2:2] add_4_c_o, add_5_c_o;

  Add add_1 (.a(A_0), .b(A_1), .c_i(A_2), .s(add_1_s[0]), .c_o(add_1_s[1]));
  Add add_2 (.a(A_3), .b(A_4), .c_i(A_5), .s(add_2_s[0]), .c_o(add_2_s[1]));
  Add add_3 (.a(A_6), .b(A_7), .c_i(A_8), .s(add_3_s[0]), .c_o(add_3_s[1]));
  Add #(.Bits(2)) add_4 (.a(add_1_s), .b(add_2_s), .c_i(1'b0), .s(add_4_s), .c_o(add_4_c_o[2]));
  Add #(.Bits(2)) add_5 (.a(2'b00), .b(add_3_s), .c_i(1'b0), .s(add_5_s), .c_o(add_5_c_o[2]));
  Add #(.Bits(3)) add_6 (.a({add_4_c_o[2], add_4_s}), .b({add_5_c_o[2], add_5_s}), .c_i(1'b0), .s(S[2:0]), .c_o(S[3]));
endmodule
