// Digital circuit check_diagonal.dig as structural Verilog
module check_diagonal (
  input  [1:0] I_0,
  input  S_0,
  input  [1:0] I_1,
  input  [1:0] I_2,
  input  [1:0] I_3,
  input  [1:0] I_4,
  input  [1:0] I_5,
  input  [1:0] I_6,
  input  [1:0] I_7,
  input  [1:0] I_8,
  input  S_1,
  input  S_2,
  input  S_3,
  input  S_4,
  input  S_5,
  input  S_6,
  input  S_7,
  input  S_8,
  output _1pnt,
  output _5pnt
);

  wire _0_1_eq, _0_3_eq, _0_4_eq, _1_2_eq, _1_4_eq, _2_4_eq, _2_5_eq, _3_4_eq, _3_6_eq, _4_5_eq, _4_6_eq,
       _4_7_eq, _4_8_eq, _5_8_eq, _6_7_eq, _7_8_eq, and_1_out, and_2_out, and_3_out, and_4_out, and_5_out,
       and_6_out, and_7_out, and_8_out, and_9_out, and_10_out, and_11_out, and_12_out, and_13_out,
       and_14_out, and_15_out, and_16_out, and_17_out, and_18_out, compare3_1_eq, compare3_2_eq,
       compare3_3_eq, compare3_4_eq, compare3_5_eq, compare3_6_eq, compare3_7_eq, compare3_8_eq, or_1_out,
       or_2_out, or_3_out, or_4_out, or_5_out, or_6_out, or_7_out, or_8_out, or_9_out, or_12_out, or_13_out,
       or_14_out, or_15_out, or_16_out, or_17_out, or_18_out, or_19_out, or_20_out;

  Comparator #(.Bits(2)) _0_1 (.a(I_0), .b(I_1), .eq(_0_1_eq));  // open: gt, lt
  Comparator #(.Bits(2)) _0_4 (.a(I_4), .b(I_0), .eq(_0_4_eq));  // open: gt, lt
  Comparator #(.Bits(2)) _0_3 (.a(I_0), .b(I_3), .eq(_0_3_eq));  // open: gt, lt
  Comparator #(.Bits(2)) _1_2 (.a(I_1), .b(I_2), .eq(_1_2_eq));  // open: gt, lt
  Comparator #(.Bits(2)) _2_4 (.a(I_2), .b(I_4), .eq(_2_4_eq));  // open: gt, lt
  Comparator #(.Bits(2)) _1_4 (.a(I_1), .b(I_4), .eq(_1_4_eq));  // open: gt, lt
  Comparator #(.Bits(2)) _2_5 (.a(I_2), .b(I_5), .eq(_2_5_eq));  // open: gt, lt
  or or_1 (or_1_out, _0_1_eq, _0_4_eq, _0_3_eq);
  or or_2 (or_2_out, _0_1_eq, _1_2_eq, _1_4_eq);
  or or_3 (or_3_out, _1_2_eq, _2_4_eq, _2_5_eq);
  or or_4 (or_4_out, _0_3_eq, _3_4_eq, _3_6_eq);
  or or_5 (or_5_out, _0_4_eq, _2_4_eq, _1_4_eq, _3_4_eq, _4_6_eq, _4_5_eq, _4_8_eq, _4_7_eq);
  or or_6 (or_6_out, _2_5_eq, _4_5_eq, _5_8_eq);
  or or_7 (or_7_out, _4_6_eq, _3_6_eq, _6_7_eq);
  or or_8 (or_8_out, _4_7_eq, _5_8_eq, _7_8_eq);
  or or_9 (or_9_out, _4_8_eq, _5_8_eq, _7_8_eq);
  Comparator #(.Bits(2)) _3_4 (.a(I_3), .b(I_4), .eq(_3_4_eq));  // open: gt, lt
  Comparator #(.Bits(2)) _4_6 (.a(I_4), .b(I_6), .eq(_4_6_eq));  // open: gt, lt
  Comparator #(.Bits(2)) _3_6 (.a(I_3), .b(I_6), .eq(_3_6_eq));  // open: gt, lt
  and and_1 (and_1_out, S_0, or_1_out);
  and and_2 (and_2_out, S_1, or_2_out);
  and and_3 (and_3_out, S_2, or_3_out);
  and and_4 (and_4_out, S_3, or_4_out);
  and and_5 (and_5_out, S_4, or_5_out);
  and and_6 (and_6_out, S_5, or_6_out);
  and and_7 (and_7_out, S_6, or_7_out);
  and and_8 (and_8_out, S_7, or_8_out);
  and and_9 (and_9_out, S_8, or_9_out);
  Comparator #(.Bits(2)) _4_5 (.a(I_4), .b(I_5), .eq(_4_5_eq));  // open: gt, lt
  Comparator #(.Bits(2)) _4_8 (.a(I_4), .b(I_8), .eq(_4_8_eq));  // open: gt, lt
  or or_10 (_1pnt, and_1_out, and_2_out, and_3_out, and_4_out, and_5_out, and_6_out, and_7_out, and_8_out, and_9_out);
  Comparator #(.Bits(2)) _4_7 (.a(I_4), .b(I_7), .eq(_4_7_eq));  // open: gt, lt
  Comparator #(.Bits(2)) _5_8 (.a(I_5), .b(I_8), .eq(_5_8_eq));  // open: gt, lt
  Comparator #(.Bits(2)) _6_7 (.a(I_6), .b(I_7), .eq(_6_7_eq));  // open: gt, lt
  and and_10 (and_10_out, or_20_out, S_8);
  and and_11 (and_11_out, or_19_out, S_7);
  Comparator #(.Bits(2)) _7_8 (.a(I_7), .b(I_8), .eq(_7_8_eq));  // open: gt, lt
  and and_12 (and_12_out, or_18_out, S_6);
  and and_13 (and_13_out, or_17_out, S_5);
  and and_14 (and_14_out, or_16_out, S_4);
  and and_15 (and_15_out, or_15_out, S_3);
  or or_11 (_5pnt, and_18_out, and_17_out, and_16_out, and_15_out, and_14_out, and_13_out, and_12_out, and_11_out, and_10_out);
  and and_16 (and_16_out, or_14_out, S_2);
  and and_17 (and_17_out, or_13_out, S_1);
  and and_18 (and_18_out, or_12_out, S_0);
  compare3 compare3_1 (.a(I_2), .b(I_1), .c(I_0), .eq(compare3_1_eq));
  or or_12 (or_12_out, compare3_7_eq, compare3_4_eq, compare3_1_eq);
  or or_13 (or_13_out, compare3_5_eq, compare3_1_eq);
  or or_14 (or_14_out, compare3_8_eq, compare3_6_eq, compare3_1_eq);
  or or_15 (or_15_out, compare3_4_eq, compare3_2_eq);
  or or_16 (or_16_out, compare3_8_eq, compare3_7_eq, compare3_5_eq, compare3_2_eq);
  or or_17 (or_17_out, compare3_6_eq, compare3_2_eq);
  or or_18 (or_18_out, compare3_8_eq, compare3_4_eq, compare3_3_eq);
  or or_19 (or_19_out, compare3_5_eq, compare3_3_eq);
  or or_20 (or_20_out, compare3_7_eq, compare3_6_eq, compare3_3_eq);
  compare3 compare3_2 (.a(I_5), .b(I_4), .c(I_3), .eq(compare3_2_eq));
  compare3 compare3_3 (.a(I_8), .b(I_7), .c(I_6), .eq(compare3_3_eq));
  compare3 compare3_4 (.a(I_6), .b(I_3), .c(I_0), .eq(compare3_4_eq));
  compare3 compare3_5 (.a(I_7), .b(I_4), .c(I_1), .eq(compare3_5_eq));
  compare3 compare3_6 (.a(I_8), .b(I_5), .c(I_2), .eq(compare3_6_eq));
  compare3 compare3_7 (.a(I_8), .b(I_4), .c(I_0), .eq(compare3_7_eq));
  compare3 compare3_8 (.a(I_6), .b(I_4), .c(I_2), .eq(compare3_8_eq));

  // Notes on the sheet:
  //   0
  //   1
  //   2
  //   3
  //   4
  //   5
  //   6
  //   7
  //   8
  //   9
  //   10
  //   11
  //   12
  //   13
  //   14
  //   15
  //   16
endmodule
