// Digital circuit compare3.dig as structural Verilog
module compare3 (
  input  [1:0] a,
  input  [1:0] b,
  input  [1:0] c,
  output eq
);

  wire comparator_1_eq, comparator_2_eq;

  Comparator #(.Bits(2)) comparator_1 (.a(a), .b(b), .eq(comparator_1_eq));  // open: gt, lt
  Comparator #(.Bits(2)) comparator_2 (.a(b), .b(c), .eq(comparator_2_eq));  // open: gt, lt
  and and_1 (eq, comparator_1_eq, comparator_2_eq);
endmodule
