// Digital circuit main.dig as structural Verilog
module main (
  input  clk,
  input  clk_2,
  input  clk_3,
  input  clk_4,
  output out_2,
  output [1:0] out_3,
  output [3:0] out_5,
  output [3:0] Blue,
  output [3:0] Green,
  output [3:0] Green_2,
  output [3:0] Blue_2,
  output [7:0] out_12,
  output [7:0] out_13
);

  wire and_1_out, button_10_out, check_diagonal_1__1pnt, check_diagonal_1__5pnt, comparator_1_eq,
       decoder_1_out_1, decoder_1_out_2, decoder_1_out_3, decoder_2_out_1, decoder_2_out_2, decoder_2_out_3,
       decoder_3_out_1, decoder_3_out_2, decoder_3_out_3, decoder_4_out_1, decoder_4_out_2, decoder_4_out_3,
       decoder_5_out_1, decoder_5_out_2, decoder_5_out_3, decoder_6_out_1, decoder_6_out_2, decoder_6_out_3,
       decoder_7_out_1, decoder_7_out_2, decoder_7_out_3, decoder_8_out_1, decoder_8_out_2, decoder_8_out_3,
       decoder_9_out_1, decoder_9_out_2, decoder_9_out_3, demultiplexer_1_out_0, demultiplexer_1_out_1,
       demultiplexer_2_out_0, demultiplexer_2_out_1, demultiplexer_2_out_2, demultiplexer_2_out_3,
       demultiplexer_2_out_4, demultiplexer_2_out_5, demultiplexer_2_out_6, demultiplexer_2_out_7,
       demultiplexer_2_out_8, demultiplexer_3_out_0, demultiplexer_3_out_1, demultiplexer_3_out_2,
       demultiplexer_3_out_3, demultiplexer_3_out_4, demultiplexer_3_out_5, demultiplexer_3_out_6,
       demultiplexer_3_out_7, demultiplexer_3_out_8, not_1_out, or_1_out, or_2_out, or_3_out, or_4_out,
       or_5_out, or_6_out, or_7_out, or_8_out, or_9_out, or_10_out, register_11_q, register_12_q,
       register_13_q, register_14_q, register_16_q, register_17_q, register_18_q, register_19_q,
       rs_ff_as_1_q, rs_ff_as_3_nq, rs_ff_as_4_nq, rs_ff_as_5_nq, rs_ff_as_6_nq, rs_ff_as_8_nq,
       rs_ff_as_9_nq, rs_ff_as_10_nq;
  wire [0:0] register_10_q, register_15_q, rs_ff_as_2_nq, rs_ff_as_7_nq;
  wire [1:0] register_1_q, register_2_q, register_3_q, register_4_q, register_5_q, register_6_q,
       register_7_q, register_8_q, register_9_q;
  wire [1:1] button_1_out, button_2_out, button_4_out, button_5_out, button_6_out, button_7_out,
       button_8_out, button_9_out;
  wire [3:0] add_3_s, add_4_s, add_5_s, add_6_s, add_7_s, add_8_s, add_9_s, add_12_s, add_13_s, add_14_s,
       add_15_s, add_16_s, add_17_s, add_18_s, counterpreset_1_out, sub_1_s;
  wire [7:0] add_1_s, add_2_s, mul_1_mul, mul_2_mul, multiplexer_1_out, multiplexer_2_out;

  Demultiplexer demultiplexer_1 (
    .sel(out_2), .in(register_19_q), .out_0(demultiplexer_1_out_0), .out_1(demultiplexer_1_out_1));
  Multiplexer #(.Bits(8)) multiplexer_1 (
    .sel(demultiplexer_1_out_0), .in_0({8{1'b0}}), .in_1(8'h5), .out(multiplexer_1_out));
  Multiplexer #(.Bits(8)) multiplexer_2 (
    .sel(demultiplexer_1_out_1), .in_0({8{1'b0}}), .in_1(8'h5), .out(multiplexer_2_out));
  Q2_9bitCnt q2_9bitcnt_1 (
    .A_0(or_8_out), .A_1(or_5_out), .A_2(or_2_out), .A_3(or_9_out), .A_4(or_6_out), .A_5(or_3_out),
    .A_6(or_10_out), .A_7(or_7_out), .A_8(or_4_out), .S(out_5));
  // RGBLED rgbled_1: pin names not known; wires that end beside it: 1'b0, demultiplexer_1_out_0, demultiplexer_1_out_1
  or or_1 (or_1_out, button_7_out[1], button_4_out[1], button_1_out[1], button_8_out[1], button_5_out[1], button_2_out[1], button_9_out[1], button_6_out[1], out_3[1]);
  xor xor_1 (out_2, or_4_out, or_7_out, or_10_out, or_3_out, or_6_out, or_9_out, or_2_out, or_5_out, or_8_out);
  LED led_1 (.in(or_1_out));
  Seven_Seg_Hex seven_seg_hex_1 (.d(add_1_s[3:0]), .dp(1'b0));
  Add #(.Bits(8)) add_1 (.a(multiplexer_2_out), .b(out_12), .c_i(1'b0), .s(add_1_s));  // open: c_o
  Decoder #(.Selector_Bits(2)) decoder_1 (
    .sel(register_3_q), .out_1(decoder_1_out_1), .out_2(decoder_1_out_2), .out_3(decoder_1_out_3));  // open: out_0
  // RGBLED rgbled_2: pin names not known
  Button button_1 (.out(button_1_out[1]));
  Decoder #(.Selector_Bits(2)) decoder_2 (
    .sel(register_6_q), .out_1(decoder_2_out_1), .out_2(decoder_2_out_2), .out_3(decoder_2_out_3));  // open: out_0
  // RGBLED rgbled_3: pin names not known
  Button button_2 (.out(button_2_out[1]));
  Decoder #(.Selector_Bits(2)) decoder_3 (
    .sel(register_9_q), .out_1(decoder_3_out_1), .out_2(decoder_3_out_2), .out_3(decoder_3_out_3));  // open: out_0
  // RGBLED rgbled_4: pin names not known
  Button button_3 (.out(out_3[1]));
  CounterPreset #(.maxValue(4), .Bits(4)) counterpreset_1 (
    .en(1'b1), .C(clk_2), .dir(1'b0), .in(4'b0100), .ld(rs_ff_as_1_q), .clr(or_1_out),
    .out(counterpreset_1_out));  // open: ovf
  RS_FF_AS rs_ff_as_1 (.S(comparator_1_eq), .R(or_1_out), .Q(rs_ff_as_1_q));  // open: nQ
  or or_2 (or_2_out, decoder_1_out_1, decoder_1_out_2, decoder_1_out_3);
  or or_3 (or_3_out, decoder_2_out_1, decoder_2_out_2, decoder_2_out_3);
  or or_4 (or_4_out, decoder_3_out_1, decoder_3_out_2, decoder_3_out_3);
  Seven_Seg_Hex seven_seg_hex_2 (.d(add_2_s[3:0]), .dp(1'b0));
  Add #(.Bits(8)) add_2 (.a(multiplexer_1_out), .b(out_13), .c_i(1'b0), .s(add_2_s));  // open: c_o
  Sub #(.Bits(4)) sub_1 (.a(4'b0100), .b(counterpreset_1_out), .c_i(1'b0), .s(sub_1_s));  // open: c_o
  Comparator #(.Bits(4)) comparator_1 (.a(sub_1_s), .b(4'b0000), .eq(comparator_1_eq));  // open: gt, lt
  Decoder #(.Selector_Bits(2)) decoder_4 (
    .sel(register_2_q), .out_1(decoder_4_out_1), .out_2(decoder_4_out_2), .out_3(decoder_4_out_3));  // open: out_0
  Button button_4 (.out(button_4_out[1]));
  Decoder #(.Selector_Bits(2)) decoder_5 (
    .sel(register_5_q), .out_1(decoder_5_out_1), .out_2(decoder_5_out_2), .out_3(decoder_5_out_3));  // open: out_0
  Button button_5 (.out(button_5_out[1]));
  Decoder #(.Selector_Bits(2)) decoder_6 (
    .sel(register_8_q), .out_1(decoder_6_out_1), .out_2(decoder_6_out_2), .out_3(decoder_6_out_3));  // open: out_0
  Button button_6 (.out(button_6_out[1]));
  // RGBLED rgbled_5: pin names not known
  // RGBLED rgbled_6: pin names not known
  // RGBLED rgbled_7: pin names not known
  or or_5 (or_5_out, decoder_4_out_1, decoder_4_out_2, decoder_4_out_3);
  or or_6 (or_6_out, decoder_5_out_1, decoder_5_out_2, decoder_5_out_3);
  or or_7 (or_7_out, decoder_6_out_1, decoder_6_out_2, decoder_6_out_3);
  Decoder #(.Selector_Bits(2)) decoder_7 (
    .sel(register_1_q), .out_1(decoder_7_out_1), .out_2(decoder_7_out_2), .out_3(decoder_7_out_3));  // open: out_0
  Button button_7 (.out(button_7_out[1]));
  Decoder #(.Selector_Bits(2)) decoder_8 (
    .sel(register_4_q), .out_1(decoder_8_out_1), .out_2(decoder_8_out_2), .out_3(decoder_8_out_3));  // open: out_0
  Button button_8 (.out(button_8_out[1]));
  Decoder #(.Selector_Bits(2)) decoder_9 (
    .sel(register_7_q), .out_1(decoder_9_out_1), .out_2(decoder_9_out_2), .out_3(decoder_9_out_3));  // open: out_0
  Button button_9 (.out(button_9_out[1]));
  Seven_Seg_Hex seven_seg_hex_3 (.d(sub_1_s), .dp(1'b0));
  // RGBLED rgbled_8: pin names not known
  // RGBLED rgbled_9: pin names not known
  // RGBLED rgbled_10: pin names not known
  or or_8 (or_8_out, decoder_7_out_1, decoder_7_out_2, decoder_7_out_3);
  or or_9 (or_9_out, decoder_8_out_1, decoder_8_out_2, decoder_8_out_3);
  or or_10 (or_10_out, decoder_9_out_1, decoder_9_out_2, decoder_9_out_3);
  Register #(.Bits(2)) register_1 (.D({button_7_out[1], out_2}), .C(and_1_out), .en(button_7_out[1]), .Q(register_1_q));
  Demultiplexer #(.Selector_Bits(4)) demultiplexer_2 (
    .sel(out_5), .in(rs_ff_as_1_q), .out_0(demultiplexer_2_out_0), .out_1(demultiplexer_2_out_1),
    .out_2(demultiplexer_2_out_2), .out_3(demultiplexer_2_out_3), .out_4(demultiplexer_2_out_4),
    .out_5(demultiplexer_2_out_5), .out_6(demultiplexer_2_out_6), .out_7(demultiplexer_2_out_7),
    .out_8(demultiplexer_2_out_8));  // open: out_9, out_10, out_11, out_12, out_13, out_14, out_15
  Register #(.Bits(2)) register_2 (.D({button_4_out[1], out_2}), .C(and_1_out), .en(button_4_out[1]), .Q(register_2_q));
  Button button_10 (.out(button_10_out));
  Register #(.Bits(2)) register_3 (.D({button_1_out[1], out_2}), .C(and_1_out), .en(button_1_out[1]), .Q(register_3_q));
  RS_FF_AS rs_ff_as_2 (.S(demultiplexer_2_out_0), .R(button_10_out), .nQ(rs_ff_as_2_nq[0]));  // open: Q
  RS_FF_AS rs_ff_as_3 (.S(demultiplexer_2_out_2), .R(button_10_out), .nQ(rs_ff_as_3_nq));  // open: Q
  RS_FF_AS rs_ff_as_4 (.S(demultiplexer_2_out_4), .R(button_10_out), .nQ(rs_ff_as_4_nq));  // open: Q
  RS_FF_AS rs_ff_as_5 (.S(demultiplexer_2_out_8), .R(button_10_out), .nQ(rs_ff_as_5_nq));  // open: Q
  RS_FF_AS rs_ff_as_6 (.S(demultiplexer_2_out_6), .R(button_10_out), .nQ(rs_ff_as_6_nq));  // open: Q
  RS_FF_AS rs_ff_as_7 (.S(demultiplexer_2_out_1), .R(button_10_out), .nQ(rs_ff_as_7_nq[0]));  // open: Q
  RS_FF_AS rs_ff_as_8 (.S(demultiplexer_2_out_3), .R(button_10_out), .nQ(rs_ff_as_8_nq));  // open: Q
  RS_FF_AS rs_ff_as_9 (.S(demultiplexer_2_out_5), .R(button_10_out), .nQ(rs_ff_as_9_nq));  // open: Q
  RS_FF_AS rs_ff_as_10 (.S(demultiplexer_2_out_7), .R(button_10_out), .nQ(rs_ff_as_10_nq));  // open: Q
  Register #(.Bits(2)) register_4 (.D({button_8_out[1], out_2}), .C(and_1_out), .en(button_8_out[1]), .Q(register_4_q));
  Register #(.Bits(2)) register_5 (.D({button_5_out[1], out_2}), .C(and_1_out), .en(button_5_out[1]), .Q(register_5_q));
  Add #(.Bits(4)) add_3 (.a({3'b000, rs_ff_as_2_nq[0]}), .b(4'b0000), .c_i(rs_ff_as_3_nq), .s(add_3_s));  // open: c_o
  Add #(.Bits(4)) add_4 (.a({3'b000, rs_ff_as_7_nq[0]}), .b(4'b0000), .c_i(rs_ff_as_8_nq), .s(add_4_s));  // open: c_o
  Add #(.Bits(4)) add_5 (.a(add_3_s), .b(4'b0000), .c_i(rs_ff_as_4_nq), .s(add_5_s));  // open: c_o
  Add #(.Bits(4)) add_6 (.a(add_4_s), .b(4'b0000), .c_i(rs_ff_as_9_nq), .s(add_6_s));  // open: c_o
  Register #(.Bits(2)) register_6 (.D({button_2_out[1], out_2}), .C(and_1_out), .en(button_2_out[1]), .Q(register_6_q));
  Add #(.Bits(4)) add_7 (.a(add_5_s), .b(4'b0000), .c_i(rs_ff_as_5_nq), .s(add_7_s));  // open: c_o
  Add #(.Bits(4)) add_8 (.a(add_6_s), .b(4'b0000), .c_i(rs_ff_as_10_nq), .s(add_8_s));  // open: c_o
  Register #(.Bits(2)) register_7 (.D({button_9_out[1], out_2}), .C(and_1_out), .en(button_9_out[1]), .Q(register_7_q));
  Register #(.Bits(2)) register_8 (.D({button_6_out[1], out_2}), .C(and_1_out), .en(button_6_out[1]), .Q(register_8_q));
  Add #(.Bits(4)) add_9 (.a(add_7_s), .b(4'b0000), .c_i(rs_ff_as_6_nq), .s(add_9_s));  // open: c_o
  Register #(.Bits(2)) register_9 (.D({out_3[1], out_2}), .C(and_1_out), .en(out_3[1]), .Q(register_9_q));
  Multiplexer #(.Selector_Bits(4), .Bits(4)) multiplexer_3 (
    .sel(out_5), .in_0({3'b000, rs_ff_as_2_nq[0]}), .in_1({3'b000, rs_ff_as_2_nq[0]}), .in_2(add_3_s),
    .in_3(add_3_s), .in_4(add_5_s), .in_5(add_5_s), .in_6(add_7_s), .in_7(add_7_s), .in_8(add_9_s),
    .in_9(add_9_s), .in_10(add_9_s), .in_11(add_9_s), .in_12(add_9_s), .in_13(add_9_s), .in_14(add_9_s),
    .in_15(add_9_s), .out(Blue));
  Multiplexer #(.Selector_Bits(4), .Bits(4)) multiplexer_4 (
    .sel(out_5), .in_0(4'b0000), .in_1({3'b000, rs_ff_as_7_nq[0]}), .in_2({3'b000, rs_ff_as_7_nq[0]}),
    .in_3(add_4_s), .in_4(add_4_s), .in_5(add_6_s), .in_6(add_6_s), .in_7(add_8_s), .in_8(add_8_s),
    .in_9(add_8_s), .in_10(add_8_s), .in_11(add_8_s), .in_12(add_8_s), .in_13(add_8_s), .in_14(add_8_s),
    .in_15(add_8_s), .out(Green));
  Add #(.Bits(8)) add_10 (.a({4'b0000, Blue}), .b(mul_2_mul), .c_i(1'b0), .s(out_12));  // open: c_o
  and and_1 (and_1_out, clk, not_1_out);
  not not_1 (not_1_out, register_19_q);
  Add #(.Bits(8)) add_11 (.a({4'b0000, Green}), .b(mul_1_mul), .c_i(1'b0), .s(out_13));  // open: c_o
  Demultiplexer #(.Selector_Bits(4)) demultiplexer_3 (
    .sel(out_5), .in(check_diagonal_1__1pnt), .out_0(demultiplexer_3_out_0), .out_1(demultiplexer_3_out_1),
    .out_2(demultiplexer_3_out_2), .out_3(demultiplexer_3_out_3), .out_4(demultiplexer_3_out_4),
    .out_5(demultiplexer_3_out_5), .out_6(demultiplexer_3_out_6), .out_7(demultiplexer_3_out_7),
    .out_8(demultiplexer_3_out_8));  // open: out_9, out_10, out_11, out_12, out_13, out_14, out_15
  Register register_10 (.D(demultiplexer_3_out_0), .C(clk_3), .en(demultiplexer_3_out_0), .Q(register_10_q[0]));
  Register register_11 (.D(demultiplexer_3_out_2), .C(clk_3), .en(demultiplexer_3_out_2), .Q(register_11_q));
  Register register_12 (.D(demultiplexer_3_out_4), .C(clk_3), .en(demultiplexer_3_out_4), .Q(register_12_q));
  Register register_13 (.D(demultiplexer_3_out_8), .C(clk_3), .en(demultiplexer_3_out_8), .Q(register_13_q));
  Register register_14 (.D(demultiplexer_3_out_6), .C(clk_3), .en(demultiplexer_3_out_6), .Q(register_14_q));
  Register register_15 (.D(demultiplexer_3_out_1), .C(clk_3), .en(demultiplexer_3_out_1), .Q(register_15_q[0]));
  Register register_16 (.D(demultiplexer_3_out_3), .C(clk_3), .en(demultiplexer_3_out_3), .Q(register_16_q));
  Register register_17 (.D(demultiplexer_3_out_5), .C(clk_3), .en(demultiplexer_3_out_5), .Q(register_17_q));
  Register register_18 (.D(demultiplexer_3_out_7), .C(clk_3), .en(demultiplexer_3_out_7), .Q(register_18_q));
  check_diagonal check_diagonal_1 (
    .I_0(register_3_q), .S_0(button_1_out[1]), .I_1(register_2_q), .I_2(register_1_q), .I_3(register_6_q),
    .I_4(register_5_q), .I_5(register_4_q), .I_6(register_9_q), .I_7(register_8_q), .I_8(register_7_q),
    .S_1(button_4_out[1]), .S_2(button_7_out[1]), .S_3(button_2_out[1]), .S_4(button_5_out[1]),
    .S_5(button_8_out[1]), .S_6(out_3[1]), .S_7(button_6_out[1]), .S_8(button_9_out[1]),
    ._1pnt(check_diagonal_1__1pnt), ._5pnt(check_diagonal_1__5pnt));
  Add #(.Bits(4)) add_12 (.a({3'b000, register_10_q[0]}), .b(4'b0000), .c_i(register_11_q), .s(add_12_s));  // open: c_o
  Add #(.Bits(4)) add_13 (.a({3'b000, register_15_q[0]}), .b(4'b0000), .c_i(register_16_q), .s(add_13_s));  // open: c_o
  Add #(.Bits(4)) add_14 (.a(add_12_s), .b(4'b0000), .c_i(register_12_q), .s(add_14_s));  // open: c_o
  Add #(.Bits(4)) add_15 (.a(add_13_s), .b(4'b0000), .c_i(register_17_q), .s(add_15_s));  // open: c_o
  Add #(.Bits(4)) add_16 (.a(add_14_s), .b(4'b0000), .c_i(register_13_q), .s(add_16_s));  // open: c_o
  Add #(.Bits(4)) add_17 (.a(add_15_s), .b(4'b0000), .c_i(register_18_q), .s(add_17_s));  // open: c_o
  LED led_2 (.in(check_diagonal_1__1pnt));
  LED led_3 (.in(check_diagonal_1__5pnt));
  Add #(.Bits(4)) add_18 (.a(add_16_s), .b(4'b0000), .c_i(register_14_q), .s(add_18_s));  // open: c_o
  Register register_19 (.D(check_diagonal_1__5pnt), .C(clk_4), .en(check_diagonal_1__5pnt), .Q(register_19_q));
  Multiplexer #(.Selector_Bits(4), .Bits(4)) multiplexer_5 (
    .sel(out_5), .in_0({3'b000, register_10_q[0]}), .in_1({3'b000, register_10_q[0]}), .in_2(add_12_s),
    .in_3(add_12_s), .in_4(add_14_s), .in_5(add_14_s), .in_6(add_16_s), .in_7(add_16_s), .in_8(add_18_s),
    .in_9(add_18_s), .in_10(add_18_s), .in_11(add_18_s), .in_12(add_18_s), .in_13(add_18_s),
    .in_14(add_18_s), .in_15(add_18_s), .out(Green_2));
  Mul #(.Bits(4)) mul_1 (.a(4'b0010), .b(Green_2), .mul(mul_1_mul));
  Multiplexer #(.Selector_Bits(4), .Bits(4)) multiplexer_6 (
    .sel(out_5), .in_0(4'b0000), .in_1({3'b000, register_15_q[0]}), .in_2({3'b000, register_15_q[0]}),
    .in_3(add_13_s), .in_4(add_13_s), .in_5(add_15_s), .in_6(add_15_s), .in_7(add_17_s), .in_8(add_17_s),
    .in_9(add_17_s), .in_10(add_17_s), .in_11(add_17_s), .in_12(add_17_s), .in_13(add_17_s),
    .in_14(add_17_s), .in_15(add_17_s), .out(Blue_2));
  Mul #(.Bits(4)) mul_2 (.a(4'b0010), .b(Blue_2), .mul(mul_2_mul));

  assign out_3[0] = out_2;

  // Notes on the sheet:
  //   clk: Hz: 5
  //   clk_4: Hz: 5
  //   Winner
  //   Blue
  //   Press and hold the push button
  //   for atleast 1 second to play
  //   Green
  //   Timer
  //   0
  //   2
  //   1
  //   3
  //   4
  //   5
  //   6
  //   7
  //   8
  //   2 Diagonal / Straight Move
  //   BINGO!
endmodule
